// Logisim project newpro.circ as structural Verilog: 3 circuits, main circuit main
module main (
  output [15:0] out_1,
  output [3:0] out_2
);

  wire button_1_out, clock_1_out, cpu_1_jump, not_1_out, register_6_q;
  wire [15:0] counter_1_q, cpu_1_out, n16_reg_1_x1, n16_reg_1_x2, register_2_q, register_3_q, register_4_q,
       register_5_q, register_7_q;
  wire [31:0] register_1_q, rom_1_data;

  Clock clock_1 (.out(clock_1_out));
  Button button_1 (.out(button_1_out));
  Counter #(.width(16), .max('hffff)) counter_1 (
    .load(register_6_q), .D(register_7_q), .count(not_1_out), .Q(counter_1_q), .clk(clock_1_out),
    .clr(button_1_out));  // open: carry
  not not_1 (not_1_out, register_6_q);
  ROM #(.addrWidth(16), .dataWidth(32)) rom_1 (.addr(counter_1_q), .data(rom_1_data), .sel(1'b1));
  Register #(.width(32)) register_1 (
    .D(rom_1_data), .Q({register_1_q[31:8], out_2, register_1_q[3:0]}), .clk(clock_1_out), .clr(button_1_out));  // open: en
  _16_reg u_16_reg_1 (
    .NULL(register_1_q[31:16]), .Ax0(register_1_q[3:0]), .Ax1(register_1_q[15:12]), .Ax2(register_1_q[11:8]),
    .x0(register_5_q), .out_9(out_1), .ck(clock_1_out), .rst(button_1_out), .x1(n16_reg_1_x1),
    .x2(n16_reg_1_x2));  // open: Ax3, x3
  Register #(.width(16)) register_2 (
    .D(n16_reg_1_x1), .Q(register_2_q), .clk(clock_1_out), .clr(button_1_out));  // open: en
  Register #(.width(16)) register_3 (
    .D(n16_reg_1_x2), .Q(register_3_q), .clk(clock_1_out), .clr(button_1_out));  // open: en
  Register #(.width(16)) register_4 (
    .D(register_1_q[31:16]), .Q(register_4_q), .clk(clock_1_out), .clr(button_1_out));  // open: en
  CPU cpu_1 (.instruct(out_2), .R1(register_2_q), .R2(register_3_q), .out(cpu_1_out), .jump(cpu_1_jump));
  Register #(.width(16)) register_5 (
    .D(cpu_1_out), .Q(register_5_q), .clk(clock_1_out), .clr(button_1_out));  // open: en
  Register #(.width(1)) register_6 (
    .D(cpu_1_jump), .Q(register_6_q), .clk(clock_1_out), .clr(button_1_out));  // open: en
  Register #(.width(16)) register_7 (
    .D(register_4_q), .Q(register_7_q), .clk(clock_1_out), .clr(button_1_out));  // open: en
  Bit_Extender bit_extender_1 ();  // open: in, out

  // Notes on the sheet:
  //   contents of rom_1 (hex, n*v repeats v):
  //   10000 640050 51 10102 10 1 51200 70 10100 10
endmodule

module _16_reg (
  input  [15:0] NULL,
  input  [3:0] Ax0,
  input  [3:0] Ax1,
  input  [3:0] Ax2,
  input  [3:0] Ax3,
  input  [15:0] x0,
  input  ck,
  input  rst,
  output [15:0] out_9,
  output [15:0] x1,
  output [15:0] x2,
  output [15:0] x3
);

  wire decoder_1_out0, decoder_1_out1, decoder_1_out2, decoder_1_out3, decoder_1_out4, decoder_1_out5,
       decoder_1_out6, decoder_1_out7, decoder_1_out8, decoder_1_out9, decoder_1_out10, decoder_1_out11,
       decoder_1_out12, decoder_1_out13, decoder_1_out14, decoder_1_out15;
  wire [15:0] register_3_q, register_4_q, register_5_q, register_6_q, register_7_q, register_8_q,
       register_9_q, register_10_q, register_11_q, register_12_q, register_13_q, register_14_q,
       register_15_q, register_16_q;

  Decoder #(.select(4)) decoder_1 (
    .out0(decoder_1_out0), .out1(decoder_1_out1), .out2(decoder_1_out2), .out3(decoder_1_out3),
    .out4(decoder_1_out4), .out5(decoder_1_out5), .out6(decoder_1_out6), .out7(decoder_1_out7),
    .out8(decoder_1_out8), .out9(decoder_1_out9), .out10(decoder_1_out10), .out11(decoder_1_out11),
    .out12(decoder_1_out12), .out13(decoder_1_out13), .out14(decoder_1_out14), .out15(decoder_1_out15),
    .sel(Ax0));  // open: en
  Register #(.width(16)) register_1 (.D(x0), .en(decoder_1_out0), .clk(ck), .clr(rst));  // open: Q
  Register #(.width(16)) register_2 (.D(x0), .en(decoder_1_out1), .Q(out_9), .clk(ck), .clr(rst));
  Register #(.width(16)) register_3 (.D(x0), .en(decoder_1_out2), .Q(register_3_q), .clk(ck), .clr(rst));
  Register #(.width(16)) register_4 (.D(x0), .en(decoder_1_out3), .Q(register_4_q), .clk(ck), .clr(rst));
  Register #(.width(16)) register_5 (.D(x0), .en(decoder_1_out4), .Q(register_5_q), .clk(ck), .clr(rst));
  Register #(.width(16)) register_6 (.D(x0), .en(decoder_1_out5), .Q(register_6_q), .clk(ck), .clr(rst));
  Register #(.width(16)) register_7 (.D(x0), .en(decoder_1_out6), .Q(register_7_q), .clk(ck), .clr(rst));
  Register #(.width(16)) register_8 (.D(x0), .en(decoder_1_out7), .Q(register_8_q), .clk(ck), .clr(rst));
  Register #(.width(16)) register_9 (.D(x0), .en(decoder_1_out8), .Q(register_9_q), .clk(ck), .clr(rst));
  Register #(.width(16)) register_10 (.D(x0), .en(decoder_1_out9), .Q(register_10_q), .clk(ck), .clr(rst));
  Register #(.width(16)) register_11 (.D(x0), .en(decoder_1_out10), .Q(register_11_q), .clk(ck), .clr(rst));
  Register #(.width(16)) register_12 (.D(x0), .en(decoder_1_out11), .Q(register_12_q), .clk(ck), .clr(rst));
  Register #(.width(16)) register_13 (.D(x0), .en(decoder_1_out12), .Q(register_13_q), .clk(ck), .clr(rst));
  Register #(.width(16)) register_14 (.D(x0), .en(decoder_1_out13), .Q(register_14_q), .clk(ck), .clr(rst));
  Register #(.width(16)) register_15 (.D(x0), .en(decoder_1_out14), .Q(register_15_q), .clk(ck), .clr(rst));
  Register #(.width(16)) register_16 (.D(x0), .en(decoder_1_out15), .Q(register_16_q), .clk(ck), .clr(rst));
  Multiplexer #(.select(4), .width(16)) multiplexer_1 (
    .in0(NULL), .in1(out_9), .in2(register_3_q), .in3(register_4_q), .in4(register_5_q), .in5(register_6_q),
    .in6(register_7_q), .in7(register_8_q), .in8(register_9_q), .in9(register_10_q), .in10(register_11_q),
    .in11(register_12_q), .in12(register_13_q), .in13(register_14_q), .in14(register_15_q),
    .in15(register_16_q), .out(x1), .sel(Ax1));  // open: en
  Multiplexer #(.select(4), .width(16)) multiplexer_2 (
    .in0(NULL), .in1(out_9), .in2(register_3_q), .in3(register_4_q), .in4(register_5_q), .in5(register_6_q),
    .in6(register_7_q), .in7(register_8_q), .in8(register_9_q), .in9(register_10_q), .in10(register_11_q),
    .in11(register_12_q), .in12(register_13_q), .in13(register_14_q), .in14(register_15_q),
    .in15(register_16_q), .out(x2), .sel(Ax2));  // open: en
  Multiplexer #(.select(4), .width(16)) multiplexer_3 (
    .in0(NULL), .in1(out_9), .in2(register_3_q), .in3(register_4_q), .in4(register_5_q), .in5(register_6_q),
    .in6(register_7_q), .in7(register_8_q), .in8(register_9_q), .in9(register_10_q), .in10(register_11_q),
    .in11(register_12_q), .in12(register_13_q), .in13(register_14_q), .in14(register_15_q),
    .in15(register_16_q), .out(x3), .sel(Ax3));  // open: en
endmodule

module CPU (
  input  [3:0] instruct,
  input  [15:0] R1,
  input  [15:0] R2,
  output [15:0] out,
  output jump
);

  wire comparator_1_lt, decoder_1_out1, decoder_1_out2, decoder_1_out3, decoder_1_out4, decoder_1_out5,
       decoder_1_out6, decoder_1_out7;
  wire [15:0] adder_1_out, divider_1_out, multiplier_1_out, subtractor_1_out;

  Decoder #(.select(4)) decoder_1 (
    .out1(decoder_1_out1), .out2(decoder_1_out2), .out3(decoder_1_out3), .out4(decoder_1_out4),
    .out5(decoder_1_out5), .out6(decoder_1_out6), .out7(decoder_1_out7), .sel(instruct));  // open: out0, out8, out9, out10, out11, out12, out13, out14, out15, en
  assign out = decoder_1_out1 ? adder_1_out : 16'bz;  // Controlled_Buffer controlled_buffer_1
  Adder #(.width(16)) adder_1 (.a(R1), .b(R2), .out(adder_1_out));  // open: cin, cout
  assign out = decoder_1_out2 ? subtractor_1_out : 16'bz;  // Controlled_Buffer controlled_buffer_2
  Subtractor #(.width(16)) subtractor_1 (.a(R1), .b(R2), .out(subtractor_1_out));  // open: bin, bout
  Multiplier #(.width(16)) multiplier_1 (.a(R1), .b(R2), .out(multiplier_1_out));  // open: cin, cout
  assign out = decoder_1_out3 ? multiplier_1_out : 16'bz;  // Controlled_Buffer controlled_buffer_3
  assign out = decoder_1_out4 ? divider_1_out : 16'bz;  // Controlled_Buffer controlled_buffer_4
  Divider #(.width(16)) divider_1 (.a(R1), .b(R2), .out(divider_1_out));  // open: upper, rem
  assign out = decoder_1_out5 ? R1 : 16'bz;  // Controlled_Buffer controlled_buffer_5
  assign jump = decoder_1_out6 ? decoder_1_out6 : 1'bz;  // Controlled_Buffer controlled_buffer_6
  Comparator #(.width(16)) comparator_1 (.a(R1), .b(R2), .lt(comparator_1_lt));  // open: gt, eq
  assign jump = decoder_1_out7 ? comparator_1_lt : 1'bz;  // Controlled_Buffer controlled_buffer_7
  Pull_Resistor pull_resistor_1 (.node(out));
  Pull_Resistor pull_resistor_2 (.node(jump));
endmodule
